# Fritzing sketch enter (saved by Fritzing 0.9.3b)
breadboards: 1

parts:
  パーツ1 = Arduino Uno (Rev3)
  J3 = Infrared Proximity Sensor
  J4 = Piezo Speaker
  LED1 = LED - 5mm [color="White (4500K)" package="5 mm [THT]"]
  LED2 = RGB LED (com. cathode, rgb) [package="5 mm [THT]"]
  LED3 = LED - 5mm [color="White (4500K)" package="5 mm [THT]"]
  R1 = Resistor [tolerance=±5% resistance=75 package=THT]
  LED4 = LED - 5mm [color="Red (660nm)" package="5 mm [THT]"]
  LED5 = LED - 5mm [color="Red (660nm)" package="5 mm [THT]"]
  R2 = Resistor [tolerance=±5% resistance=150 package=THT]
  LED6 = LED - 5mm [color="Yellow (595nm)" package="5 mm [THT]"]
  LED7 = LED - 5mm [color="Yellow (595nm)" package="5 mm [THT]"]
  R3 = Resistor [tolerance=±5% resistance=150 package=THT]
  LED8 = LED - 5mm [color="Green (570nm)" package="5 mm [THT]"]
  LED9 = LED - 5mm [color="Green (570nm)" package="5 mm [THT]"]
  R4 = Resistor [tolerance=±5% resistance=150 package=THT]
  LED10 = LED - 5mm [color="Blue (525nm)" package="5 mm [THT]"]
  LED11 = LED - 5mm [color="Blue (525nm)" package="5 mm [THT]"]
  R5 = Resistor [tolerance=±5% resistance=75 package=THT]
  R6 = Resistor [tolerance=±5% resistance=150 package=THT]
  R7 = Resistor [tolerance=±5% resistance=75 package=THT]
  LED12 = RGB LED (com. cathode, rgb) [package="5 mm [THT]"]
  R8 = Resistor [tolerance=±5% resistance=150 package=THT]
  LED13 = LED - 5mm [color="Orange (620nm)" package="5 mm [THT]"]
  LED14 = LED - 5mm [color="Orange (620nm)" package="5 mm [THT]"]
  R9 = Resistor [tolerance=±5% resistance=150 package=THT]
  Q1 = QRE1113 [package=qre1113]
  R10 = Resistor [tolerance=±5% resistance=200 package=THT]

nets:
  N1: パーツ1.A0, J3.Vout
  N2: パーツ1.D8, Q1.K
  N3: パーツ1.D7, R1.Pin_0, R2.Pin_0, R3.Pin_0, R4.Pin_0, R5.Pin_0, R6.Pin_0, R7.Pin_0, R8.Pin_0, R9.Pin_0, R10.Pin_0
  5V: パーツ1.5V, J3.Vcc
  GND: パーツ1.GND, J3.GND, J4.pin1, LED1.cathode, LED2.common_cathode, LED3.cathode, LED4.cathode, LED5.cathode, LED6.cathode, LED7.cathode, LED8.cathode, LED9.cathode, LED10.cathode, LED11.cathode, LED12.common_cathode, LED14.cathode, Q1.E
  N4: J4.pin2, Q1.A
  N5: LED1.anode, LED3.anode, R1.Pin_1
  N6: LED2.red_anode, R6.Pin_1
  N7: LED2.blue_anode, R7.Pin_1, LED12.blue_anode
  N8: LED4.anode, LED5.anode, R2.Pin_1
  N9: LED6.anode, LED7.anode, R3.Pin_1
  N10: LED8.anode, LED9.anode, R4.Pin_1
  N11: LED10.anode, LED11.anode, R5.Pin_1
  N12: LED12.red_anode, LED13.cathode, R9.Pin_1
  N13: R8.Pin_1, LED13.anode, LED14.anode
